# Fritzing sketch Diagrama (saved by Fritzing 0.9.3b)
breadboards: 1

parts:
  Componente1 = Arduino Uno (Rev3)
  J2 = Basic Servo
  R1 = Rotary Potentiometer (Small) [maximum_resistance=100kΩ package=THT]

nets:
  N1: Componente1.A0, R1.wiper
  N2: Componente1.D6_PWM, J2.pulse
  5V: Componente1.5V, J2.vcc, R1.leg2
  GND: Componente1.GND, J2.gnd, R1.leg1
